// Logisim project contador assíncrono (0-89).circ as structural Verilog: 4 circuits, main circuit main
module main (
);

  wire CLOCK_out, cont2_1_a, cont2_1_b, cont2_1_c, cont2_1_d, cont2_1_zera, cont3_1_a, cont3_1_b, cont3_1_c,
       cont3_1_d, decod_1_a, decod_1_b, decod_1_c, decod_1_d, decod_1_e, decod_1_f, decod_1_g, decod_2_a,
       decod_2_b, decod_2_c, decod_2_d, decod_2_e, decod_2_f, decod_2_g;

  Clock CLOCK (.out(CLOCK_out));
  cont2 cont2_1 (.CLOCK(CLOCK_out), .A(cont2_1_a), .B(cont2_1_b), .C(cont2_1_c), .D(cont2_1_d), .ZERA(cont2_1_zera));
  cont3 cont3_1 (.CLOCK(cont2_1_zera), .A(cont3_1_a), .B(cont3_1_b), .C(cont3_1_c), .D(cont3_1_d));  // open: ZERA
  decod decod_1 (
    .in_1(cont2_1_a), .in_2(cont2_1_b), .in_3(cont2_1_c), .in_4(cont2_1_d), .A(decod_1_a), .B(decod_1_b),
    .C(decod_1_c), .D(decod_1_d), .E(decod_1_e), .F(decod_1_f), .G(decod_1_g));
  decod decod_2 (
    .in_1(cont3_1_a), .in_2(cont3_1_b), .in_3(cont3_1_c), .in_4(cont3_1_d), .A(decod_2_a), .B(decod_2_b),
    .C(decod_2_c), .D(decod_2_d), .E(decod_2_e), .F(decod_2_f), .G(decod_2_g));
  _7_Segment_Display u_7_segment_display_1 (
    .g(decod_2_g), .f(decod_2_f), .a(decod_2_a), .b(decod_2_b), .e(decod_2_e), .d(decod_2_d), .c(decod_2_c));  // open: dp
  _7_Segment_Display u_7_segment_display_2 (
    .g(decod_1_g), .f(decod_1_f), .a(decod_1_a), .b(decod_1_b), .e(decod_1_e), .d(decod_1_d), .c(decod_1_c));  // open: dp
endmodule

// CONT 0 9
module cont2 (
  input  CLOCK,
  output A,
  output B,
  output C,
  output D,
  output ZERA
);

  and and_1 (ZERA, A, C);
  T_Flip_Flop #(.trigger("falling")) t_ff_1 (.clk(CLOCK), .T(1'b1), .Q(D), .reset(ZERA));  // open: Qn, preset, en
  T_Flip_Flop #(.trigger("falling")) t_ff_2 (.clk(D), .T(1'b1), .Q(C), .reset(ZERA));  // open: Qn, preset, en
  T_Flip_Flop #(.trigger("falling")) t_ff_3 (.clk(C), .T(1'b1), .Q(B), .reset(ZERA));  // open: Qn, preset, en
  T_Flip_Flop #(.trigger("falling")) t_ff_4 (.clk(B), .T(1'b1), .Q(A), .reset(ZERA));  // open: Qn, preset, en
endmodule

// DECODIFICADOR
module decod (
  input  in_1,
  input  in_2,
  input  in_3,
  input  in_4,
  output A,
  output B,
  output C,
  output D,
  output E,
  output F,
  output G
);

  wire and_1_out, and_2_out, and_3_out, and_4_out, and_5_out, and_6_out, and_7_out, not_1_out, not_2_out,
       not_3_out, not_4_out, xnor_1_out, xnor_2_out, xor_1_out;

  not not_1 (not_1_out, in_1);
  not not_2 (not_2_out, in_2);
  not not_3 (not_3_out, in_3);
  not not_4 (not_4_out, in_4);
  xnor xnor_1 (xnor_1_out, in_2, in_4);
  xnor xnor_2 (xnor_2_out, in_3, in_4);
  and and_1 (and_1_out, not_2_out, not_4_out);
  and and_2 (and_2_out, not_2_out, in_3);
  and and_3 (and_3_out, in_3, not_4_out);
  and and_4 (and_4_out, in_2, not_3_out, in_4);
  and and_5 (and_5_out, not_3_out, not_4_out);
  and and_6 (and_6_out, in_2, not_3_out);
  and and_7 (and_7_out, in_2, not_4_out);
  xor xor_1 (xor_1_out, in_2, in_3);
  or or_1 (A, in_1, xnor_1_out, in_3);
  or or_2 (B, not_2_out, xnor_2_out);
  or or_3 (C, in_2, not_3_out, in_4);
  or or_4 (D, in_1, and_1_out, and_2_out, and_3_out, and_4_out);
  or or_5 (E, and_1_out, and_3_out);
  or or_6 (F, in_1, and_5_out, and_6_out, and_7_out);
  or or_7 (G, xor_1_out, in_1, and_3_out);
endmodule

// CONT 0 8
module cont3 (
  input  CLOCK,
  output A,
  output B,
  output C,
  output D,
  output ZERA
);

  and and_1 (ZERA, A, D);
  T_Flip_Flop #(.trigger("falling")) t_ff_1 (.clk(CLOCK), .T(1'b1), .Q(D), .reset(ZERA));  // open: Qn, preset, en
  T_Flip_Flop #(.trigger("falling")) t_ff_2 (.clk(D), .T(1'b1), .Q(C), .reset(ZERA));  // open: Qn, preset, en
  T_Flip_Flop #(.trigger("falling")) t_ff_3 (.clk(C), .T(1'b1), .Q(B), .reset(ZERA));  // open: Qn, preset, en
  T_Flip_Flop #(.trigger("falling")) t_ff_4 (.clk(B), .T(1'b1), .Q(A), .reset(ZERA));  // open: Qn, preset, en
endmodule
