// Logisim project contador síncrono.circ as structural Verilog: 2 circuits, main circuit main
module main (
  input  PONTO
);

  wire a, b, c, clock_1_out, d, e, f, g, Q0, Q0_prime, Q1, Q1_prime, Q2, Q2_prime, Q2_prime_Q1_prime_Q0_out,
       Q2_Q1, Q3, Q3_Q0_prime_out, Q3_Q1_out;

  Clock clock_1 (.out(clock_1_out));
  or Q3_Q0_prime (Q3_Q0_prime_out, Q3, Q0_prime);
  or Q3_Q1 (Q3_Q1_out, Q3, Q1);
  and u_Q2_Q1 (Q2_Q1, Q2, Q1);
  and Q2_prime_Q1_prime_Q0 (Q2_prime_Q1_prime_Q0_out, Q2_prime, Q1_prime, Q0);
  J_K_Flip_Flop u_Q3 (
    .J(Q2_prime_Q1_prime_Q0_out), .clk(clock_1_out), .K(1'b1), .Q(Q3));  // open: Qn, preset, en, reset
  not not_1 (Q2_prime, Q2);
  J_K_Flip_Flop u_Q2 (.J(Q3_Q1_out), .clk(clock_1_out), .K(1'b1), .Q(Q2));  // open: Qn, preset, en, reset
  J_K_Flip_Flop u_Q1 (.J(Q3_Q0_prime_out), .clk(clock_1_out), .K(1'b1), .Q(Q1));  // open: Qn, preset, en, reset
  not not_2 (Q1_prime, Q1);
  not not_3 (Q0_prime, Q0);
  J_K_Flip_Flop u_Q0 (.J(1'b1), .clk(clock_1_out), .K(Q2_Q1), .Q(Q0));  // open: Qn, preset, en, reset
  _7_Segment_Display u_7_segment_display_1 (.g(g), .f(f), .a(a), .b(b), .e(e), .d(d), .c(c), .dp(PONTO));
  decodificador decodificador_1 (
    .in_1(Q3), .in_2(Q2), .in_3(Q1), .in_4(Q0), .out_5(a), .out_6(b), .out_7(c), .out_8(d), .out_9(e),
    .out_10(f), .out_11(g));

  // Other names for the same wires on the sheet: tunnel = PONTO

  // Notes on the sheet:
  //   CIRCUITO LÓGICO
  //   CONTADOR SÍNCRONO - [0, 3, 5, 1, 9, 7]
  //   DECODIFICADOR 'BINÁRIO-DECIMAL'
  //   DISPLAY DE 7 SEGMENTOS
endmodule

// DECODIFICADOR
module decodificador (
  input  in_1,
  input  in_2,
  input  in_3,
  input  in_4,
  output out_5,
  output out_6,
  output out_7,
  output out_8,
  output out_9,
  output out_10,
  output out_11
);

  wire and_1_out, and_2_out, and_3_out, and_4_out, and_5_out, and_6_out, and_7_out, and_8_out, and_9_out,
       and_10_out, not_1_out, not_2_out, not_3_out, xnor_1_out, xnor_2_out, xor_1_out;

  not not_1 (not_1_out, in_2);
  not not_2 (not_2_out, in_4);
  not not_3 (not_3_out, in_3);
  xnor xnor_1 (xnor_1_out, in_2, in_4);
  xnor xnor_2 (xnor_2_out, in_3, in_4);
  and and_1 (and_1_out, not_1_out, not_2_out);
  and and_2 (and_2_out, not_1_out, in_3);
  and and_3 (and_3_out, in_3, not_2_out);
  and and_4 (and_4_out, in_2, not_3_out, in_4);
  and and_5 (and_5_out, not_1_out, not_2_out);
  and and_6 (and_6_out, in_3, not_2_out);
  and and_7 (and_7_out, not_3_out, not_2_out);
  and and_8 (and_8_out, in_2, not_3_out);
  and and_9 (and_9_out, in_2, not_2_out);
  xor xor_1 (xor_1_out, in_2, in_3);
  and and_10 (and_10_out, in_3, not_2_out);
  or or_1 (out_5, xnor_1_out, in_1, in_3);
  or or_2 (out_6, xnor_2_out, not_1_out);
  or or_3 (out_7, in_2, not_3_out, in_4);
  or or_4 (out_8, in_1, and_1_out, and_2_out, and_3_out, and_4_out);
  or or_5 (out_9, and_5_out, and_6_out);
  or or_6 (out_10, in_1, and_7_out, and_8_out, and_9_out);
  or or_7 (out_11, in_1, xor_1_out, and_10_out);
endmodule
