// Logisim project decodificador.circ as structural Verilog: 1 circuit, main circuit decodificador
module decodificador (
  input  A,
  input  B,
  input  C,
  input  D,
  output a_2,
  output b_2,
  output c_2,
  output d_2,
  output e,
  output f,
  output g
);

  wire and_1_out, and_2_out, and_3_out, and_4_out, and_5_out, and_6_out, and_7_out, and_8_out, and_9_out,
       and_10_out, not_1_out, not_2_out, not_3_out, xnor_1_out, xnor_2_out, xor_1_out;

  not not_1 (not_1_out, B);
  not not_2 (not_2_out, C);
  not not_3 (not_3_out, D);
  and and_1 (and_1_out, not_1_out, not_3_out);
  and and_2 (and_2_out, not_1_out, C);
  and and_3 (and_3_out, C, not_3_out);
  and and_4 (and_4_out, B, not_2_out, D);
  and and_5 (and_5_out, not_1_out, not_3_out);
  and and_6 (and_6_out, C, not_3_out);
  and and_7 (and_7_out, not_2_out, not_3_out);
  and and_8 (and_8_out, B, not_2_out);
  and and_9 (and_9_out, B, not_3_out);
  and and_10 (and_10_out, C, not_3_out);
  xnor xnor_1 (xnor_1_out, B, D);
  xnor xnor_2 (xnor_2_out, C, D);
  xor xor_1 (xor_1_out, B, C);
  or or_1 (a_2, xnor_1_out, A, C);
  or or_2 (b_2, xnor_2_out, not_1_out);
  or or_3 (c_2, B, not_2_out, D);
  or or_4 (d_2, A, and_1_out, and_2_out, and_3_out, and_4_out);
  or or_5 (e, and_5_out, and_6_out);
  or or_6 (f, A, and_7_out, and_8_out, and_9_out);
  or or_7 (g, A, xor_1_out, and_10_out);
endmodule
