// Logisim project ex 9.circ as structural Verilog: 1 circuit, main circuit main
module main (
  input  A,
  input  B,
  input  C,
  input  D
);

  wire and_1_out, and_2_out, and_3_out, nor_1_out, nor_2_out, nor_3_out, nor_4_out, not_1_out, not_2_out,
       not_3_out, not_4_out, or_1_out;

  not not_1 (not_1_out, A);
  not not_2 (not_2_out, C);
  not not_3 (not_3_out, B);
  not not_4 (not_4_out, D);
  nor nor_1 (nor_1_out, A, C);
  nor nor_2 (nor_2_out, not_3_out, not_2_out, not_4_out);
  nor nor_3 (nor_3_out, not_1_out, B, C);
  and and_1 (and_1_out, A, not_3_out, C);
  and and_2 (and_2_out, nor_1_out, not_3_out);
  and and_3 (and_3_out, nor_2_out, nor_3_out);
  nor nor_4 (nor_4_out, C, and_3_out);
  or or_1 (or_1_out, and_1_out, and_2_out, nor_4_out);

  // Notes on the sheet:
  //   _
endmodule
